# Fritzing sketch schematic (saved by Fritzing 0.8.7b)
breadboards: 1

parts:
  パーツ1 = Arduino Uno (Rev3)
  R1 = Resistor [tolerance=±5% resistance=10 package=THT]  # not connected
  R2 = Resistor [tolerance=±5% resistance=3.3 package=THT]  # not connected
  D1 = Rectifier Diode [part_number=1N4001 package="300 mil [THT]"]
  C1 = Ceramic Capacitor [capacitance=10nF package="100 mil [THT, multilayer]"]
  R3 = Resistor [tolerance=±5% resistance=1M package=THT]
  C2 = Ceramic Capacitor [capacitance=0.1nF package="100 mil [THT, multilayer]"]

nets:
  N1: パーツ1.A0, D1.anode, R3.Pin_0, C2.1
  N2: パーツ1.GND, C2.0
  N3: D1.cathode, C1.1
